// Logisim project A2_Group3.circ as structural Verilog: 1 circuit, main circuit main
module main (
  input  S2,
  input  S1,
  input  S0,
  input  A3,
  input  A2,
  input  A1,
  input  A0,
  input  B3,
  input  B2,
  input  B1,
  input  B0,
  output C,
  output V,
  output S,
  output Z,
  output O3,
  output O2,
  output O1,
  output O0
);

  wire n7408_1_pin3, n7408_1_pin6, n7408_1_pin8, n7408_1_pin11, n7432_1_pin3, n7432_1_pin6, n7432_1_pin8,
       n7432_1_pin11, n7432_2_pin3, n7432_2_pin6, n7432_2_pin8, n7432_2_pin11, n7432_3_pin5, n7432_3_pin11,
       n7432_4_pin1, n7432_4_pin6, n7432_4_pin8, n7432_4_pin10, n7486_1_pin1, n7486_1_pin2, n74266_1_pin3,
       n74266_1_pin6, n74266_1_pin8, n74266_1_pin11, n74283_1_pin1, n74283_1_pin7, n74283_1_pin9,
       n74283_1_pin14, n74283_1_pin15, n74283_2_pin15;

  _74266 u_74266_1 (
    .pin1(S0), .pin2(B2), .pin3(n74266_1_pin3), .pin4(S0), .pin5(B3), .pin6(n74266_1_pin6), .pin13(S0),
    .pin12(B0), .pin11(n74266_1_pin11), .pin10(B1), .pin9(S0), .pin8(n74266_1_pin8));
  _7408 u_7408_1 (
    .pin1(n74266_1_pin3), .pin2(S1), .pin3(n7408_1_pin3), .pin4(n74266_1_pin6), .pin5(S1),
    .pin6(n7408_1_pin6), .pin13(n74266_1_pin11), .pin12(S1), .pin11(n7408_1_pin11), .pin10(n74266_1_pin8),
    .pin9(S1), .pin8(n7408_1_pin8));
  _7432 u_7432_1 (
    .pin1(n7408_1_pin3), .pin2(A2), .pin3(n7432_1_pin3), .pin4(B2), .pin5(S0), .pin6(n7432_1_pin6),
    .pin13(n7408_1_pin11), .pin12(A0), .pin11(n7432_1_pin11), .pin10(B0), .pin9(S0), .pin8(n7432_1_pin8));
  _7432 u_7432_2 (
    .pin1(n7408_1_pin6), .pin2(A3), .pin3(n7432_2_pin3), .pin4(B3), .pin5(S0), .pin6(n7432_2_pin6),
    .pin13(n7408_1_pin8), .pin12(A1), .pin11(n7432_2_pin11), .pin10(B1), .pin9(S0), .pin8(n7432_2_pin8));
  // Probe on n7432_1_pin11
  // Probe on n7432_1_pin8
  // Probe on n7432_2_pin11
  // Probe on n7432_2_pin8
  // Probe on n7432_2_pin6
  // Probe on n7432_2_pin3
  // Probe on n7432_1_pin6
  // Probe on n7432_1_pin3
  _74283 u_74283_1 (
    .pin1(n74283_1_pin1), .pin4(O2), .pin5(n7432_1_pin3), .pin6(n7432_1_pin6), .pin7(n74283_1_pin7),
    .pin15(n74283_1_pin15), .pin14(n74283_1_pin14), .pin12(n7432_2_pin3), .pin11(n7432_2_pin6), .pin10(O3),
    .pin9(n74283_1_pin9));  // open: pin2, pin3, pin13
  _7486 u_7486_1 (
    .pin1(n7486_1_pin1), .pin2(n7486_1_pin2), .pin3(Z), .pin13(n74283_1_pin1), .pin12(n74283_1_pin9),
    .pin11(V), .pin10(n74283_1_pin9), .pin9(S1), .pin8(C));  // open: pin4, pin5, pin6
  _7432 u_7432_3 (
    .pin4(O0), .pin5(n7432_3_pin5), .pin6(n7486_1_pin2), .pin13(O2), .pin12(O3), .pin11(n7432_3_pin11),
    .pin10(n7432_3_pin11), .pin9(O1), .pin8(n7432_3_pin5));  // open: pin1, pin2, pin3
  _7432 u_7432_4 (
    .pin1(n7432_4_pin1), .pin2(S1), .pin3(n74283_1_pin7), .pin4(S2), .pin5(S1), .pin6(n7432_4_pin6),
    .pin13(n74283_1_pin1), .pin12(S1), .pin11(n74283_1_pin14), .pin10(n7432_4_pin10), .pin9(S1),
    .pin8(n7432_4_pin8));
  _74283 u_74283_2 (
    .pin1(n7432_4_pin10), .pin4(O0), .pin5(n7432_1_pin11), .pin6(n7432_1_pin8), .pin7(n7432_4_pin6),
    .pin15(n74283_2_pin15), .pin14(n7432_4_pin8), .pin12(n7432_2_pin11), .pin11(n7432_2_pin8), .pin10(O1),
    .pin9(n7432_4_pin1));  // open: pin2, pin3, pin13

  assign S = O3;
  // also tied to VCC on the sheet: {n7486_1_pin1, n74283_1_pin15, n74283_2_pin15}

  // Notes on the sheet:
  //   s0
  //   s1
  //   s2
  //   Top Pins form FA3
  //   cin3
  //   Bottom pins form FA2
  //   cout2
  //   cout2
  //   cout3 = Real
  //   cin2
  //   This IC handles Carry
  //   Cout-1
  //   cout0
  //   cout1
  //   cin1
  //   Top pins form FA1
  //   Botton pins form FA0
  //   cin0
endmodule
