// Logisim project floating_point_adder.circ as structural Verilog: 1 circuit, main circuit Main
module Main (
  input  [31:0] floatA,
  input  [31:0] floatB,
  output [31:0] result,
  output overflow,
  output underflow
);

  wire fracnum_adder_1_fracoverflow, full_pre_adder_1_are_sign_same, full_pre_adder_1_larger_sign;
  wire [9:0] full_pre_adder_1_larger_exp;
  wire [31:0] fracnum_adder_1_outputfrac, full_pre_adder_1_larger_frac, full_pre_adder_1_smaller_frac;

  full_pre_adder full_pre_adder_1 (
    .float_A(floatA), .float_B(floatB), .are_sign_same(full_pre_adder_1_are_sign_same),
    .larger_sign(full_pre_adder_1_larger_sign), .larger_exp(full_pre_adder_1_larger_exp),
    .larger_frac(full_pre_adder_1_larger_frac), .smaller_frac(full_pre_adder_1_smaller_frac));
  // Probe on full_pre_adder_1_larger_frac
  // Probe on full_pre_adder_1_smaller_frac
  fracnum_adder fracnum_adder_1 (
    .LargerFrac(full_pre_adder_1_larger_frac), .SmallerFrac(full_pre_adder_1_smaller_frac),
    .is_sign_same(full_pre_adder_1_are_sign_same), .OutputFrac(fracnum_adder_1_outputfrac),
    .FracOverflow(fracnum_adder_1_fracoverflow));
  // Probe on fracnum_adder_1_outputfrac
  // Probe on full_pre_adder_1_larger_exp
  Normalizer normalizer_1 (
    .totalData(fracnum_adder_1_outputfrac), .exponent(full_pre_adder_1_larger_exp),
    .largestSign(full_pre_adder_1_larger_sign), .carryOut(fracnum_adder_1_fracoverflow),
    .truncatedFloatingPoint(result), .overflow(overflow), .underflow(underflow));
endmodule
