// Logisim project phase1_pre_add.circ as structural Verilog: 7 circuits, main circuit full_pre_adder
module exp_frac_comparator (
  input  [20:0] A_frac,
  input  [9:0] A_exp,
  input  [20:0] B_frac,
  input  [9:0] B_exp,
  output A_lt_B,
  output A_gte_B
);

  wire comparator_1_eq, comparator_1_gt;

  Comparator #(.mode("unsigned"), .width(31)) comparator_1 (
    .a({A_exp, A_frac}), .b({B_exp, B_frac}), .gt(comparator_1_gt), .eq(comparator_1_eq), .lt(A_lt_B));
  _7432 u_7432_1 (
    .pin1(comparator_1_gt), .pin2(comparator_1_eq), .pin3(A_gte_B));  // open: pin4, pin5, pin6, pin13, pin12, pin11, pin10, pin9, pin8
endmodule

module is_signs_same (
  input  sign_1,
  input  sign_2,
  output is_sign_same
);

  _74266 u_74266_1 (
    .pin1(sign_1), .pin2(sign_2), .pin3(is_sign_same));  // open: pin4, pin5, pin6, pin13, pin12, pin11, pin10, pin9, pin8
endmodule

module frac_to_sig_21_to_32 (
  input  [20:0] bits_21,
  input  [9:0] exp,
  output [31:0] bits_32
);

  Priority_Encoder #(.select(4)) priority_encoder_1 (
    .in0(exp[0]), .in1(exp[1]), .in2(exp[2]), .in3(exp[3]), .in4(exp[4]), .in5(exp[5]), .in6(exp[6]),
    .in7(exp[7]), .in8(exp[8]), .in9(exp[9]), .gs(bits_32[31]));  // open: in10, in11, in12, in13, in14, in15, out, en_out, en_in

  assign bits_32[30:0] = {bits_21, {10{1'b0}}};
endmodule

module super_mux (
  input  is_A_lt_B,
  input  A_sign,
  input  B_sign,
  input  [9:0] A_exp,
  input  [9:0] B_exp,
  input  [20:0] A_frac,
  input  [20:0] B_frac,
  output larger_sign,
  output [9:0] larger_exp,
  output [20:0] larger_frac,
  output [9:0] smaller_exp,
  output [20:0] smaller_frac
);

  Multiplexer multiplexer_1 (.in0(A_sign), .in1(B_sign), .out(larger_sign), .sel(is_A_lt_B));
  Multiplexer #(.width(10)) multiplexer_2 (.in0(A_exp), .in1(B_exp), .out(larger_exp), .sel(is_A_lt_B));
  Multiplexer #(.width(21)) multiplexer_3 (.in0(A_frac), .in1(B_frac), .out(larger_frac), .sel(is_A_lt_B));
  Multiplexer #(.width(10)) multiplexer_4 (.in0(B_exp), .in1(A_exp), .out(smaller_exp), .sel(is_A_lt_B));
  Multiplexer #(.width(21)) multiplexer_5 (.in0(B_frac), .in1(A_frac), .out(smaller_frac), .sel(is_A_lt_B));
endmodule

module exp_to_difference (
  input  [9:0] larger_exp,
  input  [9:0] smaller_exp,
  output [9:0] diff_exp
);

  Subtractor #(.width(10)) subtractor_1 (.a(larger_exp), .b(smaller_exp), .out(diff_exp));  // open: bin, bout
endmodule

module shift_smaller_frac (
  input  [31:0] smaller_sig,
  input  [9:0] diff_exp,
  output [31:0] shifted_smaller_frac
);

  wire n7432_1_pin3, n7432_1_pin6, n7432_1_pin11, n7432_1_pin12;
  wire [31:0] multiplexer_1_out;

  Multiplexer #(.width(32)) multiplexer_1 (
    .in0(smaller_sig), .in1({32{1'b0}}), .out(multiplexer_1_out), .sel(n7432_1_pin11));
  Shifter #(.shift("lr"), .width(32)) shifter_1 (
    .in(multiplexer_1_out), .\dist (diff_exp[4:0]), .out(shifted_smaller_frac));
  _7432 u_7432_1 (
    .pin1(diff_exp[5]), .pin2(diff_exp[6]), .pin3(n7432_1_pin3), .pin4(n7432_1_pin3), .pin5(diff_exp[7]),
    .pin6(n7432_1_pin6), .pin13(diff_exp[9]), .pin12(n7432_1_pin12), .pin11(n7432_1_pin11),
    .pin10(diff_exp[8]), .pin9(n7432_1_pin6), .pin8(n7432_1_pin12));
endmodule

module full_pre_adder (
  input  [31:0] float_A,
  input  [31:0] float_B,
  output are_sign_same,
  output larger_sign,
  output [9:0] larger_exp,
  output [31:0] larger_sig,
  output [31:0] smaller_sig
);

  wire exp_frac_comparator_1_a_lt_b;
  wire [9:0] exp_to_difference_1_diff_exp, super_mux_1_smaller_exp;
  wire [20:0] super_mux_1_larger_frac, super_mux_1_smaller_frac;
  wire [31:0] frac_to_sig_21_to_32_2_bits_32;

  // Probe on float_A[31]
  // Probe on float_A[30:21]
  // Probe on float_A[20:0]
  // Probe on float_B[31]
  // Probe on float_B[30:21]
  // Probe on float_B[20:0]
  exp_frac_comparator exp_frac_comparator_1 (
    .A_frac(float_A[20:0]), .A_exp(float_A[30:21]), .B_frac(float_B[20:0]), .B_exp(float_B[30:21]),
    .A_lt_B(exp_frac_comparator_1_a_lt_b));  // open: A_gte_B
  is_signs_same is_signs_same_1 (.sign_1(float_A[31]), .sign_2(float_B[31]), .is_sign_same(are_sign_same));
  super_mux super_mux_1 (
    .is_A_lt_B(exp_frac_comparator_1_a_lt_b), .A_sign(float_A[31]), .B_sign(float_B[31]),
    .A_exp(float_A[30:21]), .B_exp(float_B[30:21]), .A_frac(float_A[20:0]), .B_frac(float_B[20:0]),
    .larger_sign(larger_sign), .larger_exp(larger_exp), .larger_frac(super_mux_1_larger_frac),
    .smaller_exp(super_mux_1_smaller_exp), .smaller_frac(super_mux_1_smaller_frac));
  frac_to_sig_21_to_32 frac_to_sig_21_to_32_1 (
    .bits_21(super_mux_1_larger_frac), .exp(larger_exp), .bits_32(larger_sig));
  frac_to_sig_21_to_32 frac_to_sig_21_to_32_2 (
    .bits_21(super_mux_1_smaller_frac), .exp(super_mux_1_smaller_exp),
    .bits_32(frac_to_sig_21_to_32_2_bits_32));
  exp_to_difference exp_to_difference_1 (
    .larger_exp(larger_exp), .smaller_exp(super_mux_1_smaller_exp), .diff_exp(exp_to_difference_1_diff_exp));
  shift_smaller_frac shift_smaller_frac_1 (
    .smaller_sig(frac_to_sig_21_to_32_2_bits_32), .diff_exp(exp_to_difference_1_diff_exp),
    .shifted_smaller_frac(smaller_sig));
  // Probe on super_mux_1_larger_frac
  // Probe on super_mux_1_smaller_frac
  // Probe on frac_to_sig_21_to_32_2_bits_32
  // Probe on exp_to_difference_1_diff_exp
  // Probe on smaller_sig
endmodule
