// Logisim project phase2_add.circ as structural Verilog: 1 circuit, main circuit fracnum_adder
module fracnum_adder (
  input  [31:0] larger_sig,
  input  [31:0] smaller_sig,
  input  is_sign_same,
  output [31:0] output_sig,
  output sig_overflow
);

  wire adder_1_cout;
  wire [31:0] adder_1_out, subtractor_1_out;

  Subtractor #(.width(32)) subtractor_1 (.a(larger_sig), .b(smaller_sig), .out(subtractor_1_out));  // open: bin, bout
  Adder #(.width(32)) adder_1 (.a(larger_sig), .b(smaller_sig), .out(adder_1_out), .cout(adder_1_cout));  // open: cin
  _7408 u_7408_1 (
    .pin13(is_sign_same), .pin12(adder_1_cout), .pin11(sig_overflow));  // open: pin1, pin2, pin3, pin4, pin5, pin6, pin10, pin9, pin8
  Multiplexer #(.width(32)) multiplexer_1 (
    .in0(subtractor_1_out), .in1(adder_1_out), .out(output_sig), .sel(is_sign_same));
endmodule
