// Logisim project phase3_post_add.circ as structural Verilog: 3 circuits, main circuit Normalizer
module Normalizer (
  input  [31:0] totalData,
  input  [9:0] exponent,
  input  largestSign,
  input  carryOut,
  output [31:0] truncatedFloatingPoint,
  output overflow,
  output underflow
);

  wire adder_1_cout, n7404_1_pin10, n7408_1_pin8, n7408_1_pin9, n7408_1_pin10, n7408_1_pin12, n7408_1_pin13,
       n7432_1_pin1, n7432_1_pin4, n7432_1_pin6;
  wire [4:0] priorityencoder_1_selectbit;
  wire [9:0] adder_2_out, multiplexer_1_out, multiplexer_2_out, subtractor_2_out;
  wire [31:0] multiplexer_3_out, multiplexer_4_out, shifter_1_out, shifter_2_out;

  _7408 u_7408_1 (
    .pin13(n7408_1_pin13), .pin12(n7408_1_pin12), .pin11(underflow), .pin10(n7408_1_pin10),
    .pin9(n7408_1_pin9), .pin8(n7408_1_pin8));  // open: pin1, pin2, pin3, pin4, pin5, pin6
  // Probe on truncatedFloatingPoint[30:21]
  // Probe on truncatedFloatingPoint[20:0]
  Subtractor #(.width(10)) subtractor_1 (.a(multiplexer_2_out), .b(10'h1), .bout(n7408_1_pin12));  // open: out, bin
  _7404 u_7404_1 (
    .pin13(n7408_1_pin10), .pin12(n7408_1_pin13), .pin11(n7408_1_pin9), .pin10(n7404_1_pin10));  // open: pin1, pin2, pin3, pin4, pin5, pin6, pin9, pin8
  Adder #(.width(10)) adder_1 (.a(multiplexer_2_out), .b(10'h1), .cout(adder_1_cout));  // open: out, cin
  Shifter #(.shift("lr"), .width(32)) shifter_1 (.in(totalData), .\dist (5'b00001), .out(shifter_1_out));
  _7432 u_7432_1 (
    .pin1(n7432_1_pin1), .pin2(adder_1_cout), .pin3(overflow), .pin4(n7432_1_pin4), .pin5(n7408_1_pin8),
    .pin6(n7432_1_pin6));  // open: pin13, pin12, pin11, pin10, pin9, pin8
  PriorityEncoder priorityencoder_1 (
    .dataBus(totalData), .selectBit(priorityencoder_1_selectbit), .is_sig_zero(n7408_1_pin10));
  Adder #(.width(10)) adder_2 (.a(exponent), .b(10'h1), .out(adder_2_out));  // open: cin, cout
  // Probe on shifter_2_out
  Shifter #(.width(32)) shifter_2 (.in(totalData), .\dist (priorityencoder_1_selectbit), .out(shifter_2_out));
  // Probe on {1'b1, shifter_1_out[30:0]}
  Truncer truncer_1 (
    .in32bit(multiplexer_4_out), .inExp(multiplexer_2_out), .out21bit(truncatedFloatingPoint[20:0]),
    .outExp(truncatedFloatingPoint[30:21]), .overflow(n7432_1_pin1));
  // Probe on subtractor_2_out
  Subtractor #(.width(10)) subtractor_2 (
    .a(exponent), .b({{5{1'b0}}, priorityencoder_1_selectbit}), .out(subtractor_2_out));  // open: bin, bout
  Subtractor #(.width(10)) subtractor_3 (.a(exponent), .b(10'h1), .bout(n7408_1_pin9));  // open: out, bin
  // Probe on subtractor_2_out
  Multiplexer #(.width(10)) multiplexer_1 (
    .in0(subtractor_2_out), .in1(adder_2_out), .out(multiplexer_1_out), .sel(carryOut));
  Multiplexer #(.width(10)) multiplexer_2 (
    .in0(multiplexer_1_out), .in1({10{1'b0}}), .out(multiplexer_2_out), .sel(n7432_1_pin6));
  Multiplexer #(.width(32)) multiplexer_3 (
    .in0(shifter_2_out), .in1({1'b1, shifter_1_out[30:0]}), .out(multiplexer_3_out), .sel(carryOut));
  Multiplexer #(.width(32)) multiplexer_4 (
    .in0(multiplexer_3_out), .in1({32{1'b0}}), .out(multiplexer_4_out), .sel(n7432_1_pin6));
  _7408 u_7408_2 (
    .pin13(n7408_1_pin10), .pin12(n7404_1_pin10), .pin11(n7432_1_pin4));  // open: pin1, pin2, pin3, pin4, pin5, pin6, pin10, pin9, pin8

  assign truncatedFloatingPoint[31] = largestSign;

  // Notes on the sheet:
  //   if exp is zero but signifincant is not zero, underflow triggers
  //   is_sig_not_zero
  //   is_exp_zero
  //   maximum number reserved for infinity. overflow triggers when exp is max-1
  //   incremented exp
  //   decremented exp
  //   left shifted significant
  //   right shifted significant with MSB set to 1
  //   if adder produced carry, incremented exp with right shifted significant is selected
endmodule

module PriorityEncoder (
  input  [31:0] dataBus,
  output [4:0] selectBit,
  output is_sig_zero
);

  wire priority_encoder_1_gs;
  wire [4:0] multiplexer_1_out, priority_encoder_1_out;

  Priority_Encoder #(.select(5)) priority_encoder_1 (
    .in0(dataBus[0]), .in1(dataBus[1]), .in2(dataBus[2]), .in3(dataBus[3]), .in4(dataBus[4]),
    .in5(dataBus[5]), .in6(dataBus[6]), .in7(dataBus[7]), .in8(dataBus[8]), .in9(dataBus[9]),
    .in10(dataBus[10]), .in11(dataBus[11]), .in12(dataBus[12]), .in13(dataBus[13]), .in14(dataBus[14]),
    .in15(dataBus[15]), .in16(dataBus[16]), .in17(dataBus[17]), .in18(dataBus[18]), .in19(dataBus[19]),
    .in20(dataBus[20]), .in21(dataBus[21]), .in22(dataBus[22]), .in23(dataBus[23]), .in24(dataBus[24]),
    .in25(dataBus[25]), .in26(dataBus[26]), .in27(dataBus[27]), .in28(dataBus[28]), .in29(dataBus[29]),
    .in30(dataBus[30]), .in31(dataBus[31]), .out(priority_encoder_1_out), .gs(priority_encoder_1_gs));  // open: en_out, en_in
  Multiplexer #(.width(5)) multiplexer_1 (
    .in0({5{1'b0}}), .in1(priority_encoder_1_out), .out(multiplexer_1_out), .sel(priority_encoder_1_gs));
  _7404 u_7404_1 (
    .pin13(priority_encoder_1_gs), .pin12(is_sig_zero));  // open: pin1, pin2, pin3, pin4, pin5, pin6, pin11, pin10, pin9, pin8
  Subtractor #(.width(5)) subtractor_1 (.a({5{1'b1}}), .b(multiplexer_1_out), .out(selectBit));  // open: bin, bout
endmodule

module Truncer (
  input  [31:0] in32bit,
  input  [9:0] inExp,
  output [20:0] out21bit,
  output [9:0] outExp,
  output overflow
);

  wire adder_3_cout, n7432_1_pin1, n7432_1_pin2, n7432_1_pin3, n7432_2_pin1, n7432_2_pin2, n7432_2_pin3,
       n7432_2_pin6, n7432_3_pin8, n7432_3_pin11;
  wire [9:0] multiplexer_1_out;
  wire [20:0] adder_3_out, multiplexer_2_out;

  // Probe on in32bit[31]
  _7432 u_7432_1 (
    .pin1(n7432_1_pin1), .pin2(n7432_1_pin2), .pin3(n7432_1_pin3), .pin13(in32bit[0]), .pin12(in32bit[1]),
    .pin11(n7432_1_pin1), .pin10(in32bit[2]), .pin9(in32bit[3]), .pin8(n7432_1_pin2));  // open: pin4, pin5, pin6
  _7432 u_7432_2 (
    .pin1(n7432_2_pin1), .pin2(n7432_2_pin2), .pin3(n7432_2_pin3), .pin4(n7432_2_pin3), .pin5(n7432_1_pin3),
    .pin6(n7432_2_pin6), .pin13(in32bit[4]), .pin12(in32bit[5]), .pin11(n7432_2_pin1), .pin10(in32bit[6]),
    .pin9(in32bit[7]), .pin8(n7432_2_pin2));
  _7432 u_7432_3 (
    .pin13(n7432_2_pin6), .pin12(in32bit[10]), .pin11(n7432_3_pin11), .pin10(n7432_3_pin11),
    .pin9(in32bit[8]), .pin8(n7432_3_pin8));  // open: pin1, pin2, pin3, pin4, pin5, pin6
  Multiplexer #(.width(10)) multiplexer_1 (.in0({10{1'b0}}), .in1(10'h1), .out(multiplexer_1_out), .sel(adder_3_cout));
  Multiplexer #(.width(21)) multiplexer_2 (.in0({21{1'b0}}), .in1(21'h1), .out(multiplexer_2_out), .sel(n7432_3_pin8));
  Adder #(.width(10)) adder_1 (.a(multiplexer_1_out), .b(inExp), .out(outExp));  // open: cin, cout
  Adder #(.width(10)) adder_2 (.a(outExp), .b(10'h1), .cout(overflow));  // open: out, cin
  Adder #(.width(21)) adder_3 (
    .a(in32bit[30:10]), .b(multiplexer_2_out), .out(adder_3_out), .cout(adder_3_cout));  // open: cin
  Multiplexer #(.width(21)) multiplexer_3 (.in0(in32bit[30:10]), .in1(adder_3_out), .out(out21bit), .sel(in32bit[9]));

  // Notes on the sheet:
  //   guard
  //   round
  //   sticky 0-7
  //   when sticky, round are 0, frac LSB tells if fraction needs to be made even.
  //   Rounding up will produce carry only when all fraction bits are 1. After rounding up, they'll all be 0, so simply incrementing the exponent keeping the fractions unshifted - will produce correct result.
  //   is_sticky
  //   maximum number of bitspace reserved for inifinity. overflow triggers at max-1
  //   maximum number reserved for infinity. overflow triggers at max-1
  //   truncated frac
  //   is_sticky_or_round_or_fraclsb
  //   rounded up frac
  //   if guard: round up; else: truncate
endmodule
