// Logisim project offline3.circ as structural Verilog: 11 circuits, main circuit main
module main (
  output [3:0] out_1,
  output [2:0] out_2,
  output [3:0] out_3,
  output [3:0] out_4,
  output [3:0] out_5,
  output [3:0] out_6,
  output [3:0] out_7,
  output [3:0] out_8,
  output [3:0] out_9,
  output [3:0] Data,
  output [3:0] out_11,
  output [3:0] out_12
);

  wire alu_1_overflow, CLK_out, control_unit_1_alusrc, control_unit_1_brancheq, control_unit_1_branchnoteq,
       control_unit_1_jump, control_unit_1_memread, control_unit_1_memtoreg, control_unit_1_memwrite,
       control_unit_1_regdst, control_unit_1_regwrite, n7408_1_pin2, n7408_1_pin3, n7408_1_pin4,
       n7408_1_pin5, n7408_1_pin6, n7408_1_pin9, n7432_1_pin4, n7432_1_pin5, n7432_1_pin6;
  wire [3:0] Instructions_data;
  wire [7:0] adder83_1_sum, adder83_2_sum, bit_extender_1_out, bit_extender_2_out, eightbitmux_1_y,
       eightbitmux_2_y, register_1_q;

  Register register_1 (.D(eightbitmux_2_y), .en(CLK_out), .clk(CLK_out), .Q(register_1_q));  // open: clr
  ROM #(.dataWidth(16)) Instructions (.addr(register_1_q), .data({out_1, out_4, out_6, Instructions_data}));
  Clock CLK (.out(CLK_out));
  FourBitMUX fourbitmux_1 (.S(control_unit_1_regdst), .A0(out_6), .A1(Instructions_data), .Y(out_7));
  Adder83 adder83_1 (.A(register_1_q), .B(8'h1), .SUM(adder83_1_sum));  // open: Cin, Cout
  control_unit control_unit_1 (
    .in_1(out_1), .RegDst(control_unit_1_regdst), .Jump(control_unit_1_jump),
    .BranchEq(control_unit_1_brancheq), .BranchNotEq(control_unit_1_branchnoteq),
    .MemRead(control_unit_1_memread), .MemToReg(control_unit_1_memtoreg), .MemWrite(control_unit_1_memwrite),
    .ALUOp(out_2), .ALUSrc(control_unit_1_alusrc), .RegWrite(control_unit_1_regwrite));
  assign bit_extender_1_out = {{4{Instructions_data[3]}}, Instructions_data};  // Bit_Extender bit_extender_1
  Registers registers_1 (
    .Read1(out_4), .Read2(out_6), .WriteData(out_12), .RegWrite(control_unit_1_regwrite),
    .WriteRegister(out_7), .CLK(CLK_out), .Data1(out_3), .Data2(out_5));
  FourBitMUX fourbitmux_2 (.S(control_unit_1_alusrc), .A0(out_5), .A1(Instructions_data), .Y(out_9));
  Adder83 adder83_2 (.A(adder83_1_sum), .B(bit_extender_1_out), .SUM(adder83_2_sum));  // open: Cin, Cout
  _7432 u_7432_1 (
    .pin4(n7432_1_pin4), .pin5(n7432_1_pin5), .pin6(n7432_1_pin6));  // open: pin1, pin2, pin3, pin13, pin12, pin11, pin10, pin9, pin8
  _7408 u_7408_1 (
    .pin2(n7408_1_pin2), .pin3(n7408_1_pin3), .pin4(n7408_1_pin4), .pin5(n7408_1_pin5), .pin6(n7408_1_pin6),
    .pin13(control_unit_1_brancheq), .pin12(n7408_1_pin6), .pin11(n7432_1_pin4),
    .pin10(control_unit_1_branchnoteq), .pin9(n7408_1_pin9), .pin8(n7432_1_pin5));  // open: pin1
  _7404 u_7404_1 (
    .pin13(n7408_1_pin2), .pin12(n7408_1_pin3), .pin11(n7408_1_pin4), .pin10(n7408_1_pin5),
    .pin9(n7408_1_pin6), .pin8(n7408_1_pin9));  // open: pin1, pin2, pin3, pin4, pin5, pin6
  ALU alu_1 (.A(out_3), .B(out_9), .ALUOp(out_2), .overflow(alu_1_overflow), .Zero(n7408_1_pin6), .result(out_8));
  EightBitMUX eightbitmux_1 (.S(n7432_1_pin6), .A0(adder83_1_sum), .A1(adder83_2_sum), .Y(eightbitmux_1_y));
  assign bit_extender_2_out = {{4{1'b0}}, out_8};  // Bit_Extender bit_extender_2
  RAM #(.asyncread("true"), .dataWidth(4), .trigger("falling"), .\type ("nonvolatile")) ram_1 (
    .addr(bit_extender_2_out), .we(control_unit_1_memwrite), .oe(control_unit_1_memread), .clk(CLK_out),
    .din(out_5), .dout(Data));
  EightBitMUX eightbitmux_2 (.S(control_unit_1_jump), .A0(eightbitmux_1_y), .A1({out_4, out_6}), .Y(eightbitmux_2_y));
  FourBitMUX fourbitmux_3 (.S(control_unit_1_memtoreg), .A0(out_8), .A1(Data), .Y(out_12));

  assign out_11 = out_5;

  // Notes on the sheet:
  //   contents of Instructions (hex, n*v repeats v):
  //   9000 9000 9666 66f 23 103e d231 9234 c135 f323 b331 a431 41e0 5441 7334 f620 66f f630 66f 41d0 e131
  //   3531 8225 7630 661 2352 7620 661 41e0 6316 9000
  //   Instructions
  //   Memory
endmodule

module control_unit (
  input  [3:0] in_1,
  output RegDst,
  output Jump,
  output BranchEq,
  output BranchNotEq,
  output MemRead,
  output MemToReg,
  output MemWrite,
  output [2:0] ALUOp,
  output ALUSrc,
  output RegWrite
);

  ROM #(.addrWidth(4), .dataWidth(12)) rom_1 (
    .addr(in_1),
    .data({RegDst, Jump, BranchEq, BranchNotEq, MemRead, MemToReg, MemWrite, ALUOp, ALUSrc, RegWrite}));

  // Notes on the sheet:
  //   contents of rom_1 (hex, n*v repeats v):
  //   3 7 809 b 400 17 104 c3 f 805 204 1b 811 801 80d 22
endmodule

module ALU (
  input  [3:0] A,
  input  [3:0] B,
  input  [2:0] ALUOp,
  output overflow,
  output Zero,
  output [3:0] result
);

  wire add_1_overflow, sub_1_overflow;
  wire [3:0] add_1_sum, and_1_out, not_1_out, or_1_out, shifter_1_out, shifter_2_out, sub_1_sum;

  add add_1 (.A(A), .B(B), .sum(add_1_sum), .overflow(add_1_overflow));
  sub sub_1 (.A(A), .in_2(B), .Zero(Zero), .sum(sub_1_sum), .overflow(sub_1_overflow));
  assign and_1_out = A & B;  // AND_Gate and_1, 4 bits wide
  assign or_1_out = A | B;  // OR_Gate or_1, 4 bits wide
  Shifter #(.width(4)) shifter_1 (.in(A), .\dist (B[1:0]), .out(shifter_1_out));
  Shifter #(.shift("lr"), .width(4)) shifter_2 (.in(A), .\dist (B[1:0]), .out(shifter_2_out));
  assign not_1_out = ~or_1_out;  // NOT_Gate not_1, 4 bits wide
  Multiplexer #(.select(3)) multiplexer_1 (
    .in0(add_1_overflow), .in1(sub_1_overflow), .in2(1'b0), .in3(1'b0), .in4(1'b0), .in5(1'b0), .in6(1'b0),
    .in7(1'b0), .out(overflow), .sel(ALUOp));
  Multiplexer #(.select(3), .width(4)) multiplexer_2 (
    .in0(add_1_sum), .in1(sub_1_sum), .in2(and_1_out), .in3(or_1_out), .in4(not_1_out), .in5(shifter_1_out),
    .in6(shifter_2_out), .out(result), .sel(ALUOp));  // open: in7
endmodule

module add (
  input  [3:0] A,
  input  [3:0] B,
  output [3:0] sum,
  output overflow
);

  wire adder_1_cout, adder_2_cout;

  Adder #(.width(3)) adder_1 (.a(A[2:0]), .b(B[2:0]), .out(sum[2:0]), .cout(adder_1_cout));  // open: cin
  Adder #(.width(1)) adder_2 (.a(A[3]), .b(B[3]), .out(sum[3]), .cin(adder_1_cout), .cout(adder_2_cout));
  xor xor_1 (overflow, adder_1_cout, adder_2_cout);
endmodule

module sub (
  input  [3:0] A,
  input  [3:0] in_2,
  output Zero,
  output [3:0] sum,
  output overflow
);

  wire [3:0] negator_1_out;

  Negator #(.width(4)) negator_1 (.in(in_2), .out(negator_1_out));
  add add_1 (.A(A), .B(negator_1_out), .sum(sum), .overflow(overflow));
  nor nor_1 (Zero, sum[0], sum[1], sum[2], sum[3]);
endmodule

module FourBitMUX (
  input  S,
  input  [3:0] A0,
  input  [3:0] A1,
  output [3:0] Y
);

  // IC_74157 ic_74157_1: pin names not known; wires that end beside it: A0[0], A1[0], A0[1], A1[1], A0[2], A1[2], A0[3], A1[3], S, Y[0], Y[1], Y[2], Y[3]
endmodule

module Registers (
  input  [3:0] Read1,
  input  [3:0] Read2,
  input  [3:0] WriteData,
  input  RegWrite,
  input  [3:0] WriteRegister,
  input  CLK,
  output [3:0] Data1,
  output [3:0] Data2
);

  wire demultiplexer_1_out1, demultiplexer_1_out2, demultiplexer_1_out3, demultiplexer_1_out4,
       demultiplexer_1_out5, demultiplexer_1_out6;
  wire [3:0] sp_q, t0_q, t1_q, t2_q, t3_q, t4_q, zero_q;

  Demultiplexer #(.select(3)) demultiplexer_1 (
    .out1(demultiplexer_1_out1), .out2(demultiplexer_1_out2), .out3(demultiplexer_1_out3),
    .out4(demultiplexer_1_out4), .out5(demultiplexer_1_out5), .out6(demultiplexer_1_out6), .in(RegWrite),
    .sel(WriteRegister[2:0]));  // open: out0, out7
  Register #(.width(4)) zero (.D(4'b0000), .clk(CLK), .Q(zero_q));  // open: en, clr
  Register #(.trigger("falling"), .width(4)) t0 (
    .D(WriteData), .en(demultiplexer_1_out1), .clk(CLK), .Q(t0_q));  // open: clr
  Register #(.trigger("falling"), .width(4)) t1 (
    .D(WriteData), .en(demultiplexer_1_out2), .clk(CLK), .Q(t1_q));  // open: clr
  Register #(.trigger("falling"), .width(4)) t2 (
    .D(WriteData), .en(demultiplexer_1_out3), .clk(CLK), .Q(t2_q));  // open: clr
  Register #(.trigger("falling"), .width(4)) t3 (
    .D(WriteData), .en(demultiplexer_1_out4), .clk(CLK), .Q(t3_q));  // open: clr
  Register #(.trigger("falling"), .width(4)) t4 (
    .D(WriteData), .en(demultiplexer_1_out5), .clk(CLK), .Q(t4_q));  // open: clr
  Register #(.trigger("falling"), .width(4)) sp (
    .D(WriteData), .en(demultiplexer_1_out6), .clk(CLK), .Q(sp_q));  // open: clr
  Multiplexer #(.select(3), .width(4)) multiplexer_1 (
    .in0(zero_q), .in1(t0_q), .in2(t1_q), .in3(t2_q), .in4(t3_q), .in5(t4_q), .in6(sp_q), .out(Data1),
    .sel(Read1[2:0]));  // open: in7
  Multiplexer #(.select(3), .width(4)) multiplexer_2 (
    .in0(zero_q), .in1(t0_q), .in2(t1_q), .in3(t2_q), .in4(t3_q), .in5(t4_q), .in6(sp_q), .out(Data2),
    .sel(Read2[2:0]));  // open: in7
endmodule

module Memory (
  input  [7:0] Address,
  input  MemWrite,
  input  MemRead,
  input  CLK,
  input  [3:0] WriteData,
  output [3:0] Data
);

  RAM #(.asyncread("true"), .dataWidth(4), .trigger("falling"), .\type ("nonvolatile")) ram_1 (
    .addr(Address), .we(MemWrite), .oe(MemRead), .clk(CLK), .din(WriteData), .dout(Data));
endmodule

module Instructions (
  input  [7:0] Address,
  output [15:0] Instruction
);

  ROM #(.dataWidth(16)) rom_1 (.addr(Address), .data(Instruction));

  // Notes on the sheet:
  //   contents of rom_1 (hex, n*v repeats v):
  //   9000 9666 606 9222 223 224 f020
endmodule

module Adder83 (
  input  [7:0] A,
  input  [7:0] B,
  input  Cin,
  output Cout,
  output [7:0] SUM
);

  wire n74283_1_pin9;

  _74283 u_74283_1 (
    .pin1(SUM[1]), .pin2(B[1]), .pin3(A[1]), .pin4(SUM[0]), .pin5(A[0]), .pin6(B[0]), .pin7(Cin),
    .pin15(B[2]), .pin14(A[2]), .pin13(SUM[2]), .pin12(A[3]), .pin11(B[3]), .pin10(SUM[3]),
    .pin9(n74283_1_pin9));
  _74283 u_74283_2 (
    .pin1(SUM[5]), .pin2(B[5]), .pin3(A[5]), .pin4(SUM[4]), .pin5(A[4]), .pin6(B[4]), .pin7(n74283_1_pin9),
    .pin15(B[6]), .pin14(A[6]), .pin13(SUM[6]), .pin12(A[7]), .pin11(B[7]), .pin10(SUM[7]), .pin9(Cout));
endmodule

module EightBitMUX (
  input  S,
  input  [7:0] A0,
  input  [7:0] A1,
  output [7:0] Y
);

  FourBitMUX fourbitmux_1 (.S(S), .A0(A0[3:0]), .A1(A1[3:0]), .Y(Y[3:0]));
  FourBitMUX fourbitmux_2 (.S(S), .A0(A0[7:4]), .A1(A1[7:4]), .Y(Y[7:4]));
endmodule
